// Logisim project calculator.circ as structural Verilog
module calculadora (
  input  in_1,
  output [26:0] out_2,
  output [26:0] out_3,
  output [26:0] out_4
);

  wire _0, _1, _2, _3, _4, _5, _6, _7, _8, _9, clear, comparator_1_eq, comparator_1_gt, comparator_1_lt,
       comparator_2_eq, comparator_2_gt, comparator_2_lt, or_1_out, or_2_out, or_3_out, or_5_out, or_6_out,
       or_7_out, tunnel, tunnel_t, tunnel_t_t, tunnel_t_t_t, x, xor_1_out;
  wire [1:0] counter_1_q, op, priority_encoder_2_out;
  wire [3:0] priority_encoder_1_out;
  wire [26:0] adder_1_out, adder_2_out, bit_extender_1_out, demultiplexer_1_out0, demultiplexer_1_out1,
       divider_1_out, multiplexer_2_out, multiplier_1_out, multiplier_2_out, or_4_out, register_1_q,
       register_2_q, subtractor_1_out;
  wire [31:0] counter_2_q;

  Button u__1 (.out(_1));
  Button u__4 (.out(_4));
  Button u__7 (.out(_7));
  Button button (.out(tunnel));
  Button button_2 (.out(tunnel_t));
  Button u_x (.out(x));
  Button button_3 (.out(tunnel_t_t));
  or or_1 (or_1_out, _1, _2, _3, _4, _5, _6, _7, _8, _9, _0);
  Button u__2 (.out(_2));
  Button u__3 (.out(_3));
  Button u__5 (.out(_5));
  Button u__6 (.out(_6));
  Button u__9 (.out(_9));
  Button u__8 (.out(_8));
  Button u__0 (.out(_0));
  Button button_4 (.out(tunnel_t_t_t));
  Button u_clear (.out(clear));
  Counter #(.width(2), .max('h3)) counter_1 (
    .count(1'b1), .Q(counter_1_q), .clk(or_1_out), .clr(or_2_out));  // open: load, D, carry
  or or_2 (or_2_out, tunnel, tunnel_t, tunnel_t_t_t, x, tunnel_t_t);
  Comparator #(.width(2)) comparator_1 (
    .a(counter_1_q), .b(2'b01), .gt(comparator_1_gt), .eq(comparator_1_eq), .lt(comparator_1_lt));
  Priority_Encoder #(.select(4)) priority_encoder_1 (
    .in0(_0), .in1(_1), .in2(_2), .in3(_3), .in4(_4), .in5(_5), .in6(_6), .in7(_7), .in8(_8), .in9(_9),
    .out(priority_encoder_1_out));  // open: in10, in11, in12, in13, in14, in15, gs, en_out, en_in
  Adder #(.width(27)) adder_1 (.a(out_3), .b(out_4), .out(adder_1_out));  // open: cin, cout
  Subtractor #(.width(27)) subtractor_1 (.a(out_3), .b(out_4), .out(subtractor_1_out));  // open: bin, bout
  Multiplier #(.width(27)) multiplier_1 (.a(out_3), .b(out_4), .out(multiplier_1_out));  // open: cin, cout
  Divider #(.width(27)) divider_1 (.a(out_3), .b(out_4), .out(divider_1_out));  // open: upper, rem
  assign bit_extender_1_out = {{23{1'b0}}, priority_encoder_1_out};  // Bit_Extender bit_extender_1
  Multiplexer #(.select(2), .width(27)) multiplexer_1 (
    .in0(adder_1_out), .in1(subtractor_1_out), .in2(multiplier_1_out), .in3(divider_1_out), .out(out_2),
    .sel(op));  // open: en
  Register #(.width(27)) register_1 (.D(bit_extender_1_out), .Q(register_1_q), .clk(comparator_1_eq));  // open: en, clr
  Demultiplexer #(.width(27)) demultiplexer_1 (
    .out0(demultiplexer_1_out0), .out1(demultiplexer_1_out1), .in(register_1_q), .sel(comparator_1_lt));  // open: en
  Register #(.width(27)) register_2 (.D(bit_extender_1_out), .Q(register_2_q), .clk(comparator_1_lt));  // open: en, clr
  // Probe on out_2
  Priority_Encoder #(.select(2)) priority_encoder_2 (
    .in0(tunnel), .in1(tunnel_t), .in2(x), .in3(tunnel_t_t), .out(priority_encoder_2_out));  // open: gs, en_out, en_in
  or or_3 (or_3_out, tunnel, tunnel_t, x, tunnel_t_t);
  Multiplier #(.width(27)) multiplier_2 (
    .a(demultiplexer_1_out1), .b(27'ha), .out(multiplier_2_out));  // open: cin, cout
  assign or_4_out = demultiplexer_1_out0 | multiplier_2_out;  // OR_Gate or_4, 27 bits wide
  Register #(.width(2), .trigger("falling")) register_3 (
    .D(priority_encoder_2_out), .en(1'b1), .Q(op), .clk(or_3_out), .clr(in_1));
  Adder #(.width(27)) adder_2 (.a(or_4_out), .b(register_2_q), .out(adder_2_out));  // open: cin, cout
  // Probe on out_3
  // Probe on out_4
  Counter #(.width(32), .max('hffffffff)) counter_2 (
    .count(1'b1), .Q(counter_2_q), .clk(tunnel_t_t_t), .clr(clear));  // open: load, D, carry
  Comparator #(.width(32)) comparator_2 (
    .a(counter_2_q), .b(32'h1), .gt(comparator_2_gt), .eq(comparator_2_eq), .lt(comparator_2_lt));
  Register #(.width(27)) register_4 (.D(adder_2_out), .Q(out_4), .clk(tunnel_t_t_t), .clr(clear));  // open: en
  Multiplexer #(.width(27)) multiplexer_2 (
    .in0(adder_2_out), .in1(out_2), .out(multiplexer_2_out), .sel(comparator_2_gt));  // open: en
  or or_5 (or_5_out, tunnel, tunnel_t, xor_1_out, x, tunnel_t_t);
  or or_6 (or_6_out, comparator_2_eq, comparator_2_lt);
  or or_7 (or_7_out, or_6_out, tunnel_t_t_t);
  Register #(.width(27)) register_5 (.D(multiplexer_2_out), .Q(out_3), .clk(or_5_out), .clr(clear));  // open: en
  xor xor_1 (xor_1_out, or_6_out, or_7_out);

  // Other names for the same wires on the sheet: num1[26:0] = out_3; num2[26:0] = out_4; result[26:0] = out_2
endmodule
