// Logisim project latch.circ as structural Verilog
module latch (
  input  in_1,
  input  in_2,
  input  in_3,
  output out_4,
  output out_5
);

  wire and_1_out, and_2_out, and_3_out, and_4_out, and_5_out, and_6_out, and_7_out, and_8_out, and_9_out,
       not_1_out, not_2_out, not_3_out, not_4_out, not_5_out, not_6_out, not_7_out, not_8_out, not_9_out,
       not_10_out;

  and and_1 (and_1_out, in_2, in_3);
  and and_2 (and_2_out, in_1, and_1_out);
  and and_3 (and_3_out, and_1_out, not_1_out);
  not not_1 (not_1_out, in_1);
  not not_2 (not_2_out, in_3);
  not not_3 (not_3_out, and_2_out);
  not not_4 (not_4_out, and_3_out);
  not not_5 (not_5_out, and_4_out);
  and and_4 (and_4_out, not_3_out, not_6_out);
  and and_5 (and_5_out, not_4_out, not_5_out);
  not not_6 (not_6_out, and_5_out);
  and and_6 (and_6_out, not_5_out, not_2_out);
  and and_7 (and_7_out, not_2_out, not_7_out);
  not not_7 (not_7_out, not_5_out);
  not not_8 (not_8_out, and_6_out);
  not not_9 (not_9_out, and_7_out);
  and and_8 (and_8_out, not_9_out, out_4);
  not not_10 (not_10_out, and_8_out);
  not not_11 (out_4, and_9_out);
  and and_9 (and_9_out, not_8_out, not_10_out);
  not not_12 (out_5, out_4);

  // Notes on the sheet:
  //   LD
  //   LSR
  //   LSR
endmodule

module button (
  input  in_1,
  output out_2
);

  wire clock_1_out, latch_1_out_5;

  Clock clock_1 (.out(clock_1_out));
  latch latch_1 (.in_1(in_1), .in_2(clock_1_out), .in_3(clock_1_out), .out_5(latch_1_out_5));  // open: out_4
  latch latch_2 (.in_1(latch_1_out_5), .in_2(in_1), .in_3(clock_1_out), .out_4(out_2));  // open: out_5
endmodule

module registrador (
  input  [15:0] in_1,
  input  in_2,
  input  in_3,
  input  in_4,
  output [15:0] out_5
);

  Register #(.width(16)) register_1 (.D(in_1), .en(in_2), .Q(out_5), .clk(in_3), .clr(in_4));
endmodule
