// Logisim project primeiro.circ as structural Verilog
module novo_circuito (
  input  in_1,
  input  in_2,
  input  A,
  input  in_4,
  input  B,
  input  C,
  input  in_7,
  input  A_2,
  input  B_2,
  output out_10,
  output [1:0] A_3,
  output out_12,
  output A_4,
  output B_3
);

  wire _1, _2, _3, _4, _5, _6, _7, and_2_out, not_1_out, not_2_out, not_3_out, not_4_out, not_5_out,
       not_6_out, not_7_out, or_1_out, undriven;

  and and_1 (A_4, A_2, B_2);
  xor xor_1 (B_3, A_2, B_2);
  and and_2 (and_2_out, in_1, in_2);
  xor xor_2 (out_12, in_4, in_7);
  not not_1 (not_1_out, and_2_out);
  or or_1 (or_1_out, in_2, in_1);
  // Probe on nothing
  and and_3 (out_10, not_1_out, not_1_out, or_1_out);
  not not_2 (not_2_out, A);
  not not_3 (not_3_out, B);
  not not_4 (not_4_out, A);
  not not_5 (not_5_out, C);
  not not_6 (not_6_out, B);
  not not_7 (not_7_out, C);
  and and_4 (_1, C, B);
  and and_5 (_2, A, undriven, undriven, undriven, B);
  and and_6 (_3, C, A);
  and and_7 (_4, not_2_out, C, not_3_out);
  and and_8 (_5, not_4_out, B, not_5_out);
  and and_9 (_6, A, B, C);
  and and_10 (_7, A, not_6_out, not_7_out);
  or or_2 (A_3[0], _1, _2, _3);
  or or_3 (A_3[1], _4, _5, _6, _7);

  // Other names for the same wires on the sheet: OA = A_3[0]; OB = A_3[1]; f = A_2; g = B_2
endmodule

module calculadora (
  input  [7:0] in_1,
  input  [1:0] in_2,
  input  [7:0] in_3,
  output [7:0] out_4
);

  wire [7:0] adder_1_out, divider_1_out, multiplier_1_out, subtractor_1_out;

  Adder adder_1 (.a(in_1), .b(in_3), .out(adder_1_out));  // open: cin, cout
  Subtractor subtractor_1 (.a(in_1), .b(in_3), .out(subtractor_1_out));  // open: bin, bout
  Multiplier multiplier_1 (.a(in_1), .b(in_3), .out(multiplier_1_out));  // open: cin, cout
  Divider divider_1 (.a(in_1), .b(in_3), .out(divider_1_out));  // open: upper, rem
  Multiplexer #(.select(2), .width(8)) multiplexer_1 (
    .in0(adder_1_out), .in1(subtractor_1_out), .in2(multiplier_1_out), .in3(divider_1_out), .out(out_4),
    .sel(in_2));  // open: en

  // Other names for the same wires on the sheet: A[7:0] = in_1; B[7:0] = in_3
endmodule

module ULA (
  input  [15:0] IA,
  input  [15:0] IB,
  input  [3:0] in_3,
  output [15:0] out_4,
  output out_5,
  output out_6,
  output out_7
);

  wire [15:0] and_1_out, DIV, MULT, negator_1_out, not_1_out, or_1_out, shifter_1_out, shifter_2_out, SOMA,
       SUB, xor_1_out;

  Adder #(.width(16)) adder_1 (.a(IA), .b(IB), .out(SOMA));  // open: cin, cout
  Subtractor #(.width(16)) subtractor_1 (.a(IA), .b(IB), .out(SUB));  // open: bin, bout
  Multiplier #(.width(16)) multiplier_1 (.a(IA), .b(IB), .out(MULT));  // open: cin, cout
  Divider #(.width(16)) divider_1 (.a(IA), .b(IB), .out(DIV));  // open: upper, rem
  Shifter #(.width(16), .shift("lr")) shifter_1 (.in(IA), .\dist (IB[3:0]), .out(shifter_1_out));
  Shifter #(.width(16)) shifter_2 (.in(IA), .\dist (IB[3:0]), .out(shifter_2_out));
  Negator #(.width(16)) negator_1 (.in(IA), .out(negator_1_out));
  assign not_1_out = ~IA;  // NOT_Gate not_1, 16 bits wide
  assign and_1_out = IA & IB;  // AND_Gate and_1, 16 bits wide
  assign or_1_out = IA | IB;  // OR_Gate or_1, 16 bits wide
  assign xor_1_out = IA ^ IB;  // XOR_Gate xor_1, 16 bits wide
  Multiplexer #(.select(4), .width(16)) multiplexer_1 (
    .in0(SOMA), .in1(SUB), .in2(MULT), .in3(DIV), .in4(shifter_1_out), .in5(shifter_2_out),
    .in6(negator_1_out), .in7(not_1_out), .in8(and_1_out), .in9(or_1_out), .in10(xor_1_out), .out(out_4),
    .sel(in_3));  // open: in11, in12, in13, in14, in15, en
  Comparator #(.width(16)) comparator_1 (.a(IA), .b(IB), .gt(out_5), .eq(out_6), .lt(out_7));
endmodule
