// Logisim project ultimo.circ as structural Verilog
module ula (
  input  [15:0] IA,
  input  [15:0] IB,
  input  [3:0] in_3,
  output [15:0] out_4,
  output out_5,
  output out_6,
  output out_7
);

  wire [15:0] adder_2_out, and_1_out, DIV, MULT, negator_1_out, not_1_out, or_1_out, shifter_1_out,
       shifter_2_out, SOMA, SUB, subtractor_2_out, undriven;

  Adder #(.width(16)) adder_1 (.a(IA), .b(IB), .out(SOMA));  // open: cin, cout
  Subtractor #(.width(16)) subtractor_1 (.a(IA), .b(IB), .out(SUB));  // open: bin, bout
  Multiplier #(.width(16)) multiplier_1 (.a(IA), .b(IB), .out(MULT));  // open: cin, cout
  Divider #(.width(16)) divider_1 (.a(IA), .b(IB), .out(DIV));  // open: upper, rem
  assign and_1_out = IA & IB;  // AND_Gate and_1, 16 bits wide
  assign or_1_out = IA | IB;  // OR_Gate or_1, 16 bits wide
  assign not_1_out = ~IA;  // NOT_Gate not_1, 16 bits wide
  Negator #(.width(16)) negator_1 (.in(IA), .out(negator_1_out));
  Shifter #(.width(16)) shifter_1 (.in(IA), .\dist (IB[3:0]), .out(shifter_1_out));
  Shifter #(.width(16), .shift("lr")) shifter_2 (.in(IA), .\dist (IB[3:0]), .out(shifter_2_out));
  Adder #(.width(16)) adder_2 (.a(IA), .b(16'h1), .out(adder_2_out));  // open: cin, cout
  Subtractor #(.width(16)) subtractor_2 (.a(IA), .b(16'h1), .out(subtractor_2_out));  // open: bin, bout
  Comparator #(.width(16)) comparator_1 (.a(IA), .b(IB), .gt(out_5), .eq(out_6), .lt(out_7));
  Multiplexer #(.select(4), .width(16)) multiplexer_1 (
    .in0(and_1_out), .in1(or_1_out), .in2(not_1_out), .in3(undriven), .in4(SOMA), .in5(SUB), .in6(MULT),
    .in7(DIV), .in8(negator_1_out), .in9(shifter_1_out), .in10(shifter_2_out), .in11(adder_2_out),
    .in12(subtractor_2_out), .out(out_4), .sel(in_3));  // open: in13, in14, in15, en
endmodule

module bancoReg (
  input  in_1,
  input  in_2,
  input  in_3,
  input  [3:0] in_4,
  input  [3:0] in_5,
  input  [15:0] in_6,
  output [15:0] out_7,
  output [15:0] out_8
);

  wire clk, clock_1_out, en0, en1, en2, en3, en4, en5, en6, en7, en8, en9, en10, en11, en12, en13, en14, en15;
  wire [15:0] out0, out1, out2, out3, out4, out5, out6, out7, out8, out9, out10, out11, out12, out13, out14,
       out15;

  Clock clock_1 (.out(clock_1_out));
  or or_1 (clk, clock_1_out, in_1);
  Demultiplexer #(.select(4)) demultiplexer_1 (
    .out0(en0), .out1(en1), .out2(en2), .out3(en3), .out4(en4), .out5(en5), .out6(en6), .out7(en7),
    .out8(en8), .out9(en9), .out10(en10), .out11(en11), .out12(en12), .out13(en13), .out14(en14),
    .out15(en15), .in(in_2), .sel(in_4));  // open: en
  Register #(.width(16)) register_1 (.D(in_6), .en(en0), .Q(out0), .clk(clk), .clr(in_3));
  Register #(.width(16)) register_2 (.D(in_6), .en(en4), .Q(out4), .clk(clk), .clr(in_3));
  Register #(.width(16)) register_3 (.D(in_6), .en(en8), .Q(out8), .clk(clk), .clr(in_3));
  Register #(.width(16)) register_4 (.D(in_6), .en(en12), .Q(out12), .clk(clk), .clr(in_3));
  Register #(.width(16)) register_5 (.D(in_6), .en(en1), .Q(out1), .clk(clk), .clr(in_3));
  Register #(.width(16)) register_6 (.D(in_6), .en(en5), .Q(out5), .clk(clk), .clr(in_3));
  Register #(.width(16)) register_7 (.D(in_6), .en(en9), .Q(out9), .clk(clk), .clr(in_3));
  Register #(.width(16)) register_8 (.D(in_6), .en(en13), .Q(out13), .clk(clk), .clr(in_3));
  Multiplexer #(.select(4), .width(16)) multiplexer_1 (
    .in0(out0), .in1(out1), .in2(out2), .in3(out3), .in4(out4), .in5(out5), .in6(out6), .in7(out7),
    .in8(out8), .in9(out9), .in10(out10), .in11(out11), .in12(out12), .in13(out13), .in14(out14),
    .in15(out15), .out(out_7), .sel(in_4));  // open: en
  Register #(.width(16)) register_9 (.D(in_6), .en(en2), .Q(out2), .clk(clk), .clr(in_3));
  Register #(.width(16)) register_10 (.D(in_6), .en(en6), .Q(out6), .clk(clk), .clr(in_3));
  Register #(.width(16)) register_11 (.D(in_6), .en(en10), .Q(out10), .clk(clk), .clr(in_3));
  Register #(.width(16)) register_12 (.D(in_6), .en(en14), .Q(out14), .clk(clk), .clr(in_3));
  Multiplexer #(.select(4), .width(16)) multiplexer_2 (
    .in0(out0), .in1(out1), .in2(out2), .in3(out3), .in4(out4), .in5(out5), .in6(out6), .in7(out7),
    .in8(out8), .in9(out9), .in10(out10), .in11(out11), .in12(out12), .in13(out13), .in14(out14),
    .in15(out15), .out(out_8), .sel(in_5));  // open: en
  Register #(.width(16)) register_13 (.D(in_6), .en(en3), .Q(out3), .clk(clk), .clr(in_3));
  Register #(.width(16)) register_14 (.D(in_6), .en(en7), .Q(out7), .clk(clk), .clr(in_3));
  Register #(.width(16)) register_15 (.D(in_6), .en(en11), .Q(out11), .clk(clk), .clr(in_3));
  Register #(.width(16)) register_16 (.D(in_6), .en(en15), .Q(out15), .clk(clk), .clr(in_3));

  // Other names for the same wires on the sheet: AdressA[3:0] = in_4; AdressB[3:0] = in_5; Data[15:0] = in_6;
  //   enable = in_2; rst = in_3
endmodule

module processador (
  input  [15:0] in_1,
  output [15:0] out_2,
  output [3:0] out_3,
  output [3:0] out_4,
  output [15:0] out_5,
  output [3:0] out_6,
  output [3:0] out_7,
  output [15:0] out_8
);

  wire _1, _2, clock_1_out, comparator_1_eq, flip_flop_d_1_out_5, not_1_out, or_1_out;
  wire [3:0] multiplexer_1_out;
  wire [15:0] bit_extender_1_out, multiplexer_2_out;

  Comparator #(.width(4)) comparator_1 (.a(in_1[15:12]), .b(4'b0001), .eq(comparator_1_eq));  // open: gt, lt
  Clock clock_1 (.out(clock_1_out));
  flip_flop_d flip_flop_d_1 (
    .in_1(comparator_1_eq), .in_2(clock_1_out), .in_3(clock_1_out), .out_5(flip_flop_d_1_out_5));  // open: out_4
  ula ula_1 (.IA(out_5), .IB(out_2), .out_4(out_8), .in_3(in_1[11:8]));  // open: out_5, out_6, out_7
  or or_1 (or_1_out, _1, _2);
  flip_flop_d flip_flop_d_2 (
    .in_1(flip_flop_d_1_out_5), .in_2(comparator_1_eq), .in_3(clock_1_out), .out_4(_1));  // open: out_5
  Multiplexer #(.width(4)) multiplexer_1 (
    .in0(in_1[7:4]), .in1(in_1[11:8]), .out(multiplexer_1_out), .sel(_2));  // open: en
  Comparator #(.width(4)) comparator_2 (.a(in_1[15:12]), .b(4'b0010), .eq(_2));  // open: gt, lt
  assign bit_extender_1_out = {{12{1'b0}}, in_1[7:4]};  // Bit_Extender bit_extender_1
  bancoReg bancoreg_1 (
    .in_1(not_1_out), .in_2(or_1_out), .in_4(multiplexer_1_out), .in_5(in_1[3:0]), .in_6(multiplexer_2_out),
    .out_7(out_5), .out_8(out_2));  // open: in_3
  not not_1 (not_1_out, or_1_out);
  Multiplexer #(.width(16)) multiplexer_2 (
    .in0(bit_extender_1_out), .in1(out_8), .out(multiplexer_2_out), .sel(_1));  // open: en

  assign out_3 = in_1[3:0];
  assign out_4 = in_1[7:4];
  assign out_6 = in_1[11:8];
  assign out_7 = in_1[15:12];

  // Other names for the same wires on the sheet: Aa[15:0] = out_5; Ab[15:0] = out_2; b[3:0] = in_1[3:0];
  //   a[3:0] = in_1[7:4]; op[3:0] = in_1[11:8]; x[3:0] = in_1[15:12]; result[15:0] = out_8
endmodule

module flip_flop_d (
  input  in_1,
  input  in_2,
  input  in_3,
  output out_4,
  output out_5
);

  wire and_1_out, and_2_out, and_3_out, and_4_out, and_5_out, and_6_out, and_7_out, and_8_out, and_9_out,
       not_1_out, not_2_out, not_3_out, not_4_out, not_5_out, not_6_out, not_7_out, not_8_out, not_9_out,
       not_10_out;

  and and_1 (and_1_out, in_2, in_3);
  and and_2 (and_2_out, in_1, and_1_out);
  and and_3 (and_3_out, and_1_out, not_1_out);
  not not_1 (not_1_out, in_1);
  not not_2 (not_2_out, in_3);
  not not_3 (not_3_out, and_2_out);
  not not_4 (not_4_out, and_3_out);
  not not_5 (not_5_out, and_4_out);
  and and_4 (and_4_out, not_3_out, not_6_out);
  and and_5 (and_5_out, not_4_out, not_5_out);
  not not_6 (not_6_out, and_5_out);
  and and_6 (and_6_out, not_5_out, not_2_out);
  and and_7 (and_7_out, not_2_out, not_7_out);
  not not_7 (not_7_out, not_5_out);
  not not_8 (not_8_out, and_6_out);
  not not_9 (not_9_out, and_7_out);
  and and_8 (and_8_out, not_9_out, out_4);
  not not_10 (not_10_out, and_8_out);
  and and_9 (and_9_out, not_8_out, not_10_out);
  not not_11 (out_4, and_9_out);
  not not_12 (out_5, out_4);

  // Notes on the sheet:
  //   LD
  //   LSR
  //   LSR
endmodule
